// Logisim project Ctl_Data_Processing.circ as structural Verilog: 1 circuit, main circuit Data_Processing
module Data_Processing (
  input  Enable,
  input  [15:0] Instruction,
  output [2:0] Rd,
  output [2:0] Rn,
  output [2:0] Rm,
  output [3:0] ALU_Opcode,
  output [3:0] Flags_Update_Mask
);

  wire [3:0] multiplexer_1_out;

  BitSelector #(.group(3), .width(16)) bitselector_1 (.in(Instruction), .out(Rd), .sel(3'b000));
  BitSelector #(.group(3), .width(16)) bitselector_2 (.in(Instruction), .out(Rm), .sel(3'b001));
  Multiplexer #(.select(4), .width(4)) multiplexer_1 (
    .out(multiplexer_1_out), .sel(ALU_Opcode));  // open: in0, in1, in2, in3, in4, in5, in6, in7, in8, in9, in10, in11, in12, in13, in14, in15
  Multiplexer #(.width(4)) multiplexer_2 (
    .in0(4'b0000), .in1(multiplexer_1_out), .out(Flags_Update_Mask), .sel(Enable));

  assign Rn = Rd;

  // Other names for the same wires on the sheet: Flags[3:0] = Flags_Update_Mask; Opcode[3:0] = ALU_Opcode

  // Notes on the sheet:
  //   Choix de l'instruction
  //   Note 2: RSB instruction has Rn as 1st operand.
  //   MUL instruction has Rn as 1st operand and Rdm as 2nd operand
  //   For simplification purposes, Rm is used for 1st operand both here and in the ALU.
  //   Note: instructions that does not save the result will still have the second operand as the destination register, the ALU will copy the second register to the destination register
  //   Pull output low on Enable = 0
  //   Operandes A et B pour operation entre le contenu du registre Rdn et le contenu du registre Rm
endmodule
